# Fritzing sketch Tonuino (saved by Fritzing 0.9.3b)

parts:
  U1 = ESP32-38PinWide [part_number=ESP32-38PinWide]
  DFPlayer_Mini1 = DFPlayer MINI [package="DIP (Dual Inline) [THT]"]
  Vol_UP = Round Pushbutton
  Vol_DOWN = Round Pushbutton
  Pause/Play = Round Pushbutton
  R1 = Resistor [tolerance=±5% resistance=1k package=THT]
  SP1 = SPEAKER [package=pcb_mount_speaker]
  Bauteil1 = RFID-RC522-v2

nets:
  N1: U1.3.3, Bauteil1.3.3V
  N2: U1.GPIO25, Pause/Play.leg1
  N3: U1.GPIO26, Vol_UP.leg1
  N4: U1.GPIO27, Vol_DOWN.leg1
  N5: U1.GPIO9, DFPlayer_Mini1.TX
  N6: U1.GPIO10, R1.Pin_1
  VIN: U1.VIN, DFPlayer_Mini1.VCC
  N7: U1.GPIO4, DFPlayer_Mini1.BUSY
  N8: U1.GPIO18, Bauteil1.SCK
  N9: U1.GPIO19, Bauteil1.MISO
  GND: U1.GND, DFPlayer_Mini1.GND, Vol_UP.leg0, Vol_DOWN.leg0, Pause/Play.leg0, Bauteil1.GND
  N10: U1.GPIO21, Bauteil1.SDA
  N11: U1.GPIO22, Bauteil1.RST
  N12: U1.GPIO23, Bauteil1.MOSI
  N13: DFPlayer_Mini1.RX, R1.Pin_0
  N14: DFPlayer_Mini1.SPK1, SP1.-
  N15: DFPlayer_Mini1.SPK2, SP1.+

custom parts:
  ESP32-38PinWide: Generic 38-Pin ESP32 with wide format (only access to one side of pins on a breadboard) based on Stephen Lilley's HiLetgo ESP-WROOM-32 ESP32 ESP-32S Development Board.
  DFPlayer MINI: MP3 module by DFRobot.com for playing Music from an SD-Card. Supports WAV and MP3 files.
  RFID-RC522-v2: A simple China made RFID-RC522 Reader; do check the pin labels, as this is a MFRC522 based clone.
